# Fritzing sketch arduino sd kart mp3 mod (saved by Fritzing 0.9.2b)

parts:
  SD_card_module1 = SD Card Module
  Eleman1 = Arduino Uno (Rev3)
  SP1 = SPEAKER [package=pcb_mount_speaker]

nets:
  GND: SD_card_module1.GND, Eleman1.GND
  N1: SD_card_module1.+3.3, Eleman1.3V3
  N2: SD_card_module1.+5, Eleman1.5V
  N3: SD_card_module1.CS, Eleman1.D4
  N4: SD_card_module1.MOSI, Eleman1.D11_PWM/MOSI
  N5: SD_card_module1.SCK, Eleman1.D13/SCK
  N6: SD_card_module1.MISO, Eleman1.D12/MISO
  N7: Eleman1.D9_PWM, SP1.-

custom parts:
  SD Card Module: SD Card Module Slot Socket Reader For Arduino ARM MCU
